# Fritzing sketch 03_neopixel_LDR (saved by Fritzing 0.9.9b)
breadboards: 1

parts:
  NEOPIXEL4 = Adafruit Breadboard-Friendly NeoPixel [part_number="Adafruit #1312"]
  NEOPIXEL5 = Adafruit Breadboard-Friendly NeoPixel [part_number="Adafruit #1312"]
  R3 = Resistor [tolerance=±5% resistance=10k package="1206 [SMD]"]
  LDR = Photocell (LDR) [package=THT]
  NEOPIXEL6 = Adafruit Breadboard-Friendly NeoPixel [part_number="Adafruit #1312"]
  NeoPixel+LDR = Arduino Leonardo (Rev3b)
  LED1 = LED - 5mm [color="Red (633nm)" current=0.030 package="5 mm [THT]"]
  R4 = Resistor [tolerance=±5% power=0.25 resistance=220 package=THT]

nets (from the breadboard view):
  N1: NEOPIXEL4.IN, NEOPIXEL5.OUT
  GND: NEOPIXEL4.GND, NEOPIXEL5.GND, R3.Pin_0, NEOPIXEL6.GND, NeoPixel+LDR.GND, LED1.cathode
  VDD: NEOPIXEL4.VDD, NEOPIXEL5.VDD, LDR.pin_1, NEOPIXEL6.VDD, NeoPixel+LDR.5V
  N2: NEOPIXEL4.OUT, NeoPixel+LDR.D10_PWM/A10
  N3: NEOPIXEL5.IN, NEOPIXEL6.OUT
  N4: R3.Pin_1, LDR.pin_0, NeoPixel+LDR.A0
  N5: NeoPixel+LDR.D13_PWM, R4.Pin_0
  N6: LED1.anode, R4.Pin_1

custom parts:
  Adafruit Breadboard-Friendly NeoPixel: This is the easiest way possible to add small, bright RGB pixels to your project. We took the same technology from our Flora NeoPixels and made them breadboard friendly, with two rows of 3 x 0.1" spaced header on each side for easy soldering, chaining and breadboarding. These ultra-bright LEDs have a constant-current driver cooked right into the LED package! The pixels are chainable - so you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
