# Fritzing sketch 04_SDcard_UltrasonsicSensor_Speaker (saved by Fritzing 0.9.9b)
circuit board: 9.398cm x 7.25311cm
stripboards: 2

parts:
  UltrasonicSensor+MircoSDcardReader+Speaker = Arduino Leonardo (Rev3b)
  Mir = HC-SR04 Ultrasonic Distance Sensor
  SPKR1 = Loudspeaker

nets:
  N1: UltrasonicSensor+MircoSDcardReader+Speaker.D2/SDA, UltrasonicSensor+MircoSDcardReader+Speaker.SDA, SPKR1.pin2
  N2: UltrasonicSensor+MircoSDcardReader+Speaker.D3_PWM/SCL, Mir.ECHO
  N3: UltrasonicSensor+MircoSDcardReader+Speaker.D4/A6, Mir.TRIG
  5V: UltrasonicSensor+MircoSDcardReader+Speaker.5V, Mir.VCC
  GND: UltrasonicSensor+MircoSDcardReader+Speaker.GND, Mir.GND, SPKR1.pin1

notes:
  Fritzing and Tinkercad don't have Mirco SD Card reader, so I added into PCB.
